# Fritzing sketch Kaffee-Counter (saved by Fritzing 1.0.4)
stripboards: 1

parts:
  Mod2 = Raspberry Pi Pico W
  HW-111_RTC_(DS1307) = Adafruit DS1307 RTC Breakout [part_number="Adafruit #264"]
  PN532_(HW-147) = HW-147 PN532 NFC/RFID Module
  SD_Card_Module = SD Card Module
  BTN1 = Round Pushbutton
  BTN2 = Round Pushbutton
  BTN3 = Round Pushbutton
  LCM1602_IIC1 = LCM1602 IIC [part_number="LCM1602 IIC" chip_label="LCM1602 IIC" package="DIP (Dual Inline) [THT]"]
  LCD1 = 20x4 LCD display [part_number=2004A]
  RE1 = KY-040 Rotary encoder [package=THT]
  J1 = Piezo Speaker
  LED1 = smd LED [color="Red (633nm)" package="0603 [SMD]"]
  LED2 = smd LED [color="Blue (430nm)" package="0603 [SMD]"]
  LED3 = smd LED [color="Green (555nm)" package="0603 [SMD]"]
  Q2 = PNP-Transistor [package="TO92 [THT]"]
  Q3 = PNP-Transistor [package="TO92 [THT]"]
  Q1 = PNP-Transistor [package="TO92 [THT]"]
  RS1 = RS232 Shield

nets:
  N1: Mod2.pin_1, HW-111_RTC_(DS1307).SDA, PN532_(HW-147).SDA, LCM1602_IIC1.SDA
  N2: Mod2.pin_2, HW-111_RTC_(DS1307).SCL, PN532_(HW-147).SCL, LCM1602_IIC1.SCL
  GND: Mod2.pin_3, Mod2.pin_8, Mod2.pin_13, Mod2.pin_18, Mod2.pin_23, Mod2.pin_28, Mod2.pin_33, Mod2.pin_38, Mod2.pin_42, PN532_(HW-147).GND, SD_Card_Module.GND, BTN1.leg1, BTN2.leg1, BTN3.leg1, LCM1602_IIC1.GND, RE1.GND, J1.pin1, RS1.GND
  N3: Mod2.pin_4, BTN2.leg0
  N4: Mod2.pin_5, BTN1.leg0
  N5: Mod2.pin_6, BTN3.leg0
  N6: Mod2.pin_11, RS1.TXD
  N7: Mod2.pin_12, RS1.RXD
  N8: Mod2.pin_14, RE1.CLK
  N9: Mod2.pin_15, RE1.DT
  N10: Mod2.pin_16, RE1.SW
  N11: Mod2.pin_17, Q1.B
  N12: Mod2.pin_19, Q3.B
  N13: Mod2.pin_20, J1.pin2
  N14: Mod2.pin_24, Q2.B
  N15: Mod2.pin_29, SD_Card_Module.CS
  N16: Mod2.pin_31, SD_Card_Module.SCK
  N17: Mod2.pin_32, SD_Card_Module.MOSI
  N18: Mod2.pin_34, SD_Card_Module.MISO
  VCC: Mod2.pin_36, PN532_(HW-147).VCC, RE1.Vcc, RS1.VCC
  VCC_2: Mod2.pin_40, HW-111_RTC_(DS1307).VCC, SD_Card_Module.+5, LCM1602_IIC1.VCC
  VSS: LCM1602_IIC1.VSS, LCD1.Vss
  VDD: LCM1602_IIC1.VDD, LCD1.Vdd
  N19: LCM1602_IIC1.V0, LCD1.Vo
  N20: LCM1602_IIC1.RS, LCD1.RS
  N21: LCM1602_IIC1.RW, LCD1.R/W
  N22: LCM1602_IIC1.E, LCD1.E
  N23: LCM1602_IIC1.D0, LCD1.DB0
  N24: LCM1602_IIC1.D1, LCD1.DB1
  N25: LCM1602_IIC1.D2, LCD1.DB2
  N26: LCM1602_IIC1.D3, LCD1.DB3
  N27: LCM1602_IIC1.D4, LCD1.DB4
  N28: LCM1602_IIC1.D5, LCD1.DB5
  N29: LCM1602_IIC1.D6, LCD1.DB6
  N30: LCM1602_IIC1.D7, LCD1.DB7
  N31: LCM1602_IIC1.A, LCD1.A_+
  N32: LCM1602_IIC1.K, Q2.E, Q3.E, Q1.E
  N33: LED1.cathode, Q1.C
  N34: LED2.cathode, Q2.C
  N35: LED3.cathode, Q3.C

custom parts:
  Raspberry Pi Pico W: Raspberry Pi Pico W. Based around the RP2040 microcontroller the Pico W is a low cost microcontroller device bringing Raspberry Pi quality, cost, and easy of use to the microcontroller space. The areas marked KEEPOUT in pcb silkscreen should not have traces running through them to avoid shorts on a soldered in module!
  Adafruit DS1307 RTC Breakout: This is a great battery-backed real time clock (RTC) that allows your microcontroller project to keep track of time even if it is reprogrammed, or if the power is lost. Perfect for datalogging, clock-building, time stamping, timers and alarms, etc. The DS1307 is the most popular RTC - but it requires 5V power to work (although we've used it with 5V power and 3.3V logic successfully) PCB &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
  HW-147 PN532 NFC/RFID Module: HW-147 NFC/RFID reader module based on NXP PN532. Pins as printed on PCB: I2C header (SCL,SDA,VCC,GND) and SPI/IRQ header (SCK,MISO,MOSI,SS,VCC,GND,IRQ).
  SD Card Module: SD Card Module Slot Socket Reader For Arduino ARM MCU
  LCM1602 IIC: I2C-Module to use a 1602 or 2004 LCD on with the wire.h libory Serial LCD Modul
  20x4 LCD display: 20x4 character display. CHECK LED POLARITY BEFORE CONNECTING POWER Some versions of the dispaly have the polarity of the LED pins "A" and "K" reversed.
  KY-040 Rotary encoder: KY-040 Rotary Encoder with switch on breakout borad from AZ Delivery
  RS232 Shield: RS232 connector, 4-pin, right-angle female. Designed by Dr Kristofer Chan, King's College London / remote-research.org. Licensed under Creative Commons Attribution-ShareAlike 4.0
